# Fritzing sketch LCD_panel_fixture (saved by Fritzing 1.0.1rc)
perfboards: 1

parts:
  TRS1 = Audio Jack (TRS) 3.5mm [part_number="POT IN" package="4Ucon 08780 [THT]"]
  R1 = Slide Potentiometer [maximum_resistance=50kΩ knob_status=75% power=0W]
  TRS2 = Audio Jack (TRS) 3.5mm [part_number="CH 1" package="4Ucon 08780 [THT]"]
  TRS3 = Audio Jack (TRS) 3.5mm [package="4Ucon 08780 [THT]"]
  TRS4 = Audio Jack (TRS) 3.5mm [package="4Ucon 08780 [THT]"]
  TRS5 = Audio Jack (TRS) 3.5mm [package="4Ucon 08780 [THT]"]
  J1 = Camdenboss CTB0158-2 [part_number=CTB0158-2 package=THT]
  J2 = male pin header, 3 pins [form="♂ (male)"]
  IC1 = Voltage Regulator [part_number=step-down package=78xxl]
  TRS6 = Audio Jack (TRS) 3.5mm [package="4Ucon 08780 [THT]"]
  TRS7 = Audio Jack (TRS) 3.5mm [package="4Ucon 08780 [THT]"]
  TRS8 = Audio Jack (TRS) 3.5mm [package="4Ucon 08780 [THT]"]
  TRS9 = Audio Jack (TRS) 3.5mm [package="4Ucon 08780 [THT]"]
  J3 = male pin header, 3 pins [form="♂ (male)"]
  R2 = Resistor [tolerance=±5% power=0.25 resistance=1k package=THT]
  R3 = Resistor [tolerance=±5% power=0.25 resistance=2.2k package=THT]
  R4 = Resistor [tolerance=±5% power=0.25 resistance=2.2k package=THT]
  R5 = Resistor [tolerance=±5% power=0.25 resistance=1k package=THT]
  J4 = male pin header, 3 pins [form="♂ (male)"]
  J5 = male pin header, 3 pins [form="♂ (male)"]
  R6 = Resistor [tolerance=±5% power=0.25 resistance=2.2k package=THT]
  R8 = Resistor [tolerance=±5% power=0.25 resistance=1k package=THT]
  J6 = male pin header, 3 pins [form="♂ (male)"]
  J7 = male pin header, 3 pins [form="♂ (male)"]
  J8 = male pin header, 3 pins [form="♂ (male)"]
  J9 = male pin header, 3 pins [form="♂ (male)"]
  J16 = male pin header, 3 pins [form="♂ (male)"]
  R13 = Resistor [tolerance=±5% power=0.25 resistance=1k package=THT]
  J14 = male pin header, 3 pins [form="♂ (male)"]
  J17 = male pin header, 3 pins [form="♂ (male)"]
  J15 = male pin header, 3 pins [form="♂ (male)"]
  R12 = Resistor [tolerance=±5% power=0.25 resistance=2.2k package=THT]
  R14 = Resistor [tolerance=±5% power=0.25 resistance=2.2k package=THT]
  R15 = Resistor [tolerance=±5% power=0.25 resistance=1k package=THT]
  J18 = male pin header, 3 pins [form="♂ (male)"]
  J19 = male pin header, 3 pins [form="♂ (male)"]
  J20 = male pin header, 3 pins [form="♂ (male)"]
  J21 = male pin header, 3 pins [form="♂ (male)"]
  Composant1 = Arduino Nano (Rev3.0)

nets:
  GND: TRS1.Sleeve, R1.leg2, TRS2.Sleeve, TRS3.Sleeve, TRS4.Sleeve, TRS5.Sleeve, J1.pin2, IC1.GND, TRS6.Sleeve, TRS7.Sleeve, TRS8.Sleeve, TRS9.Sleeve, R3.Pin_0, R4.Pin_0, R6.Pin_0, R12.Pin_0, R14.Pin_0, Composant1.GND
  N1: TRS1.Ring, R1.wiper, Composant1.A0
  N2: TRS1.Tip, R1.leg1, IC1.OUT, Composant1.5V
  N3: TRS2.Ring, J3.pin2
  N4: TRS2.Tip, J2.pin2
  N5: TRS3.Ring, J5.pin2
  N6: TRS3.Tip, J4.pin2
  N7: TRS4.Ring, J9.pin2
  N8: TRS4.Tip, J7.pin2
  N9: TRS5.Ring, J6.pin2
  N10: TRS5.Tip, J8.pin2
  N11: J1.pin1, IC1.IN
  N12: J2.pin1, R3.Pin_1, R5.Pin_0, J4.pin1
  N13: J2.pin3, R5.Pin_1, J4.pin3, Composant1.D9
  N14: TRS6.Ring, J17.pin2
  N15: TRS6.Tip, J15.pin2
  N16: TRS7.Ring, J14.pin2
  N17: TRS7.Tip, J16.pin2
  N18: TRS8.Ring, J21.pin2
  N19: TRS8.Tip, J19.pin2
  N20: TRS9.Ring, J18.pin2
  N21: TRS9.Tip, J20.pin2
  N22: J3.pin1, R2.Pin_0, R4.Pin_1, J5.pin1, J6.pin1, J9.pin1, J14.pin1, J17.pin1, J18.pin1, J21.pin1
  N23: J3.pin3, R2.Pin_1, J5.pin3, J6.pin3, J9.pin3, J14.pin3, J17.pin3, J18.pin3, J21.pin3, Composant1.D12/MISO
  N24: R6.Pin_1, R8.Pin_0, J7.pin1, J8.pin1
  N25: R8.Pin_1, J7.pin3, J8.pin3, Composant1.D10
  N26: J16.pin1, R13.Pin_0, J15.pin1, R12.Pin_1
  N27: J16.pin3, R13.Pin_1, J15.pin3, Composant1.D11/MOSI
  N28: R14.Pin_1, R15.Pin_0, J19.pin1, J20.pin1
  N29: R15.Pin_1, J19.pin3, J20.pin3, Composant1.D3

notes:
  Potentiometer (optional)
  Pot input jack (optional)
  CH1 Out
  CH1 Out (optional)
  CH2 Out (optional)
  CH2 Out
  CH3 Out (optional)
  CH3 Out
  CH4 Out (optional)
  CH4 Out
  Power input
  (prefer a step-down module)
  Jumpers select output levels
  Lighting Fixture Controller
  ← 5V
  ← 3.3V
  Recommended pot ~ 50kΩ
  PWM Output
  Enable Output
  ← jacks might need an extra row
  Arduino LCD Panel
  ← 5V Regulator
  Pot and/or jack
